# Fritzing sketch technik1 (saved by Fritzing 0.9.3b)
breadboards: 1

parts:
  U1 = Mini-360 DC-DC Buck converter [part_number=MT3608 package=THT]
  U2 = Adafruit ADS1115 16Bit I2C ADC [part_number=ADS1115]
  Bat1 = battery_holder_single_18650 [part_number=BAT_18650]
  U3 = Raspberry Pi 3 [part_number=RPI-3B+]
  R1 = Resistor [tolerance=±5% resistance=10 package="1206 [SMD]"]
  R2 = Resistor [tolerance=±5% resistance=10 package="1206 [SMD]"]
  R3 = Resistor [tolerance=±5% resistance=220 package="1206 [SMD]"]
  LED1 = smd LED [color="Red (633nm)" part_number=LED_RED package="0603 [SMD]"]
  R4 = Resistor [tolerance=±5% resistance=220 package="1206 [SMD]"]
  LED2 = smd LED [color="Yellow (595nm)" part_number=LED_YELLOW package="0603 [SMD]"]
  R5 = Resistor [tolerance=±5% resistance=220 package="1206 [SMD]"]
  R6 = Resistor [tolerance=±5% resistance=220 package="1206 [SMD]"]
  LED3 = smd LED [color="Green (570nm)" part_number=LED_GREEN package="0603 [SMD]"]
  LED4 = smd LED [color="Blue (525nm)" part_number=LED_BLUE package="0603 [SMD]"]
  X1 = USB Connectors [part_number=USB-C_FEMALE package=usb-a-h]
  U4 = TP4056 [chip_label=TP4056 part_number=TP4056 package="DIP (Dual Inline) [THT]"]
  S1 = Round Pushbutton [part_number=SWITCH_BR09]
  LED5 = smd LED [color="Red (633nm)" part_number=SWITCH_LED package="0603 [SMD]"]

nets:
  N1: U1.OUT+, U3.5V
  N2: U1.OUT-, S1.leg1
  N3: U2.AIN0, R1.Pin_0, R2.Pin_0
  N4: U2.SDA, U3.GPIO2
  N5: U2.SCL, U3.GPIO3
  GND: U2.GND, U3.GND, R1.Pin_1, LED1.cathode, LED2.cathode, LED3.cathode, LED4.cathode, S1.leg0, LED5.cathode
  3V3: U2.VDD, U3.3v3, U3.3V3, LED5.anode
  N6: Bat1.+#0, R2.Pin_1, U4.pin5
  N7: Bat1.+#1, U4.pin4
  N8: U3.GPIO17, R3.Pin_0
  N9: U3.GPIO27, R4.Pin_0
  N10: U3.GPIO22, R5.Pin_0
  N11: U3.GPIO23, R6.Pin_0
  N12: R3.Pin_1, LED1.anode
  N13: R4.Pin_1, LED2.anode
  N14: R5.Pin_1, LED3.anode
  N15: R6.Pin_1, LED4.anode
  N16: X1.D+, U4.pin2
  N17: X1.GND, U4.pin1

custom parts:
  Mini-360 DC-DC Buck converter: Mini-360 DC-DC Buck converter. Tiny buck step down voltage converter, input voltage 4.75 to 23V output 1 to 17V adjustable. Available from ebay and the like.
  Adafruit ADS1115 16Bit I2C ADC: For microcontrollers without an analog-to-digital converter or when you want a higher-precision ADC, the ADS1115 provides 16-bit precision at 860 samples/second over I2C. The chip can be configured as 4 single-ended input channels, or two differential channels. As a nice bonus, it even includes a programmable gain amplifier, up to x16, to help boost up smaller single/differential signals to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
  battery_holder_single_18650: single 18650 battery holder
  TP4056: A DIP stand-in part for whatever IC you want. With 6 pins on a 300mil dual inline package (DIP) footprint.
